# Fritzing sketch wiring-diagram (saved by Fritzing 0.9.4)

parts:
  A1 = ESP32 devkit 38p expansion board
  U1 = ESP32-38PinWide [part_number=ESP32-38PinWide]  # not connected
  A2 = GY-BMP280 Breakout
  Bat1 = battery_holder_single_18650
  TP1 = TP4056 [chip_label=TP4056 package="DIP (Dual Inline) [THT]"]
  USBTTL1 = Micro USB B Plug
  M1 = INA219 DC Current Monitor Module [part_number=CJMCU]
  MOD1 = MT3608 Boost No usb
  Part1 = Solar Cell

nets:
  N1: A1.Pin_17, A1.Pin_57, M1.VCC
  N2: A1.Pin_50, A1.Pin_51, A1.Pin_52, A1.Pin_144, A2.Pin_2, A2.Pin_6, M1.GND
  N3: A1.Pin_58, A1.Pin_59, A2.Pin_1, A2.Pin_5
  N4: A1.Pin_174, A2.Pin_4, M1.SDA
  N5: A1.Pin_177, A2.Pin_3, M1.SCL
  N6: Bat1.+#0, TP1.pin5
  N7: Bat1.+#1, TP1.pin4
  N8: TP1.pin1, Part1.+
  N9: TP1.pin2, Part1.-
  N10: TP1.pin3, M1.Vin+
  N11: TP1.pin6, USBTTL1.usb, MOD1.IN_(-), MOD1.OUT_(+), MOD1.OUT_(-)
  N12: M1.Vin-, MOD1.IN_(+)

custom parts:
  ESP32 devkit 38p expansion board: Upgraded ESP32 38P Development ESP32-DevKitC-32 ESP-WROOM-32 Expansion Board.
  ESP32-38PinWide: Generic 38-Pin ESP32 with wide format (only access to one side of pins on a breadboard) based on Stephen Lilley's HiLetgo ESP-WROOM-32 ESP32 ESP-32S Development Board.
  battery_holder_single_18650: single 18650 battery holder
  TP4056: A DIP stand-in part for whatever IC you want. With 6 pins on a 300mil dual inline package (DIP) footprint.
  INA219 DC Current Monitor Module: INA219 DC Current Monitor Module Links: INA219 product information
  MT3608 Boost No usb: Chip- MT3608 / B6289 DC to DC step up, power booster module. With adjustable output voltage. Current- 2A . || Input voltage- 2V-24V || Output voltage- 5V-28V Input interface- Inversed polarity- NO. || Led indicator- No.
